# Fritzing sketch Speedtrap LCD EDITION- revised (saved by Fritzing 0.9.2b)

parts:
  MSP-EXP430G2 = TI Launchpad MSP430G2
  IR_Receiver_#1 = LED - 5mm [color="White (4500K)" package="5 mm [THT]"]
  IR_Emitter_#1 = LED - 5mm [color="Infrared (940nm)" package="5 mm [THT]"]
  IR_Emitter_#2 = LED - 5mm [color="Infrared (940nm)" package="5 mm [THT]"]
  IR_Receiver_#2 = LED - 5mm [color="White (4500K)" package="5 mm [THT]"]
  LCD1 = LCD screen
  LED1 = LED - 5mm [color="Red (633nm)" package="5 mm [THT]"]
  LED2 = LED - 5mm [color="Green (570nm)" package="5 mm [THT]"]
  5VDC_supplied_from_External_or_Launchpad = Power plug
  P2 = Trimmer Potentiometer [part_number=Brightness package=THT]
  P1 = Trimmer Potentiometer [part_number=Contrast package=THT]
  part = Trimmer Potentiometer [package=THT]  # not connected

nets:
  N1: MSP-EXP430G2.p10, LCD1.DB6
  N2: MSP-EXP430G2.p9, LCD1.DB5
  N3: MSP-EXP430G2.p8, LCD1.DB4
  N4: MSP-EXP430G2.p7, IR_Receiver_#2.cathode
  N5: MSP-EXP430G2.p6, IR_Receiver_#1.cathode
  N6: MSP-EXP430G2.p2, LED1.anode
  N7: MSP-EXP430G2.p1, IR_Emitter_#1.anode, IR_Emitter_#2.anode
  N8: MSP-EXP430G2.p11, LCD1.DB7
  N9: MSP-EXP430G2.p12, LCD1.E
  N10: MSP-EXP430G2.p13, LCD1.RS
  N11: MSP-EXP430G2.p14, LED2.anode
  VSS: MSP-EXP430G2.p20, IR_Receiver_#1.anode, IR_Emitter_#1.cathode, IR_Emitter_#2.cathode, IR_Receiver_#2.anode, LCD1.VSS, LCD1.R/W, LCD1.LED-, LED1.cathode, LED2.cathode, 5VDC_supplied_from_External_or_Launchpad.GND, P2.leg2, P1.leg2
  VDD: LCD1.VDD, 5VDC_supplied_from_External_or_Launchpad.VCC, P2.leg1, P1.leg1
  N12: LCD1.V0, P1.wiper
  N13: LCD1.LED+, P2.wiper

notes:
  IR Beam Detected Dual Direction Speed Trap Ver 1.2 LCD Edition
  Launchpad for Model Railroading, Speed Calculation & Display for Model Railroads, 1.2

custom parts:
  TI Launchpad MSP430G2: The LaunchPad is an easy-to-use, affordable, and scalable introduction to the world of microcontrollers and the MSP430 family. See: http://e2e.ti.com/group/msp430launchpad/w/default.aspx
