# Fritzing sketch Speedtrap LCD EDITION (saved by Fritzing 0.8.3b)

parts:
  Launchpad1 = TI Launchpad MSP430G2
  IR_Receiver_#1 = LED - 5mm [color="White (4500K)" package="5 mm [THT]"]
  IR_Emitter_#1 = LED - 5mm [color="Infrared (940nm)" package="5 mm [THT]"]
  IR_Emitter_#2 = LED - 5mm [color="Infrared (940nm)" package="5 mm [THT]"]
  IR_Receiver_#2 = LED - 5mm [color="White (4500K)" package="5 mm [THT]"]
  LCD1 = LCD screen
  LED1 = LED - 5mm [color="Red (633nm)" package="5 mm [THT]"]
  LED2 = LED - 5mm [color="Green (570nm)" package="5 mm [THT]"]
  5VDC_supplied_from_External_or_Launchpad = Power plug
  R2 = Trimmer Potentiometer [package=THT]
  R1 = Trimmer Potentiometer [package=THT]

nets:
  N1: Launchpad1.p10, LCD1.DB4
  N2: Launchpad1.p9, LCD1.E
  N3: Launchpad1.p8, LCD1.RS
  N4: Launchpad1.p7, IR_Receiver_#2.cathode
  N5: Launchpad1.p6, IR_Receiver_#1.cathode
  N6: Launchpad1.p2, LED1.anode
  N7: Launchpad1.p1, IR_Emitter_#1.anode, IR_Emitter_#2.anode
  N8: Launchpad1.p11, LCD1.DB5
  N9: Launchpad1.p12, LCD1.DB6
  N10: Launchpad1.p13, LCD1.DB7
  N11: Launchpad1.p14, LED2.anode
  N12: Launchpad1.p20, IR_Receiver_#1.anode, IR_Emitter_#2.cathode, IR_Receiver_#2.anode, LED1.cathode, LED2.cathode
  VSS: LCD1.VSS, LCD1.R/W, LCD1.LED-, 5VDC_supplied_from_External_or_Launchpad.GND, R2.leg1, R1.leg1
  VDD: LCD1.VDD, 5VDC_supplied_from_External_or_Launchpad.VCC, R2.leg2, R1.leg2
  N13: LCD1.V0, R2.wiper
  N14: LCD1.LED+, R1.wiper

notes:
  IR Beam Detected Dual Direction Speed Trap Ver 1.2 LCD Edition

custom parts:
  TI Launchpad MSP430G2: The LaunchPad is an easy-to-use, affordable, and scalable introduction to the world of microcontrollers and the MSP430 family. See: http://e2e.ti.com/group/msp430launchpad/w/default.aspx
